# Fritzing sketch PID_Fritzing (saved by Fritzing 0.9.3b)
breadboards: 1

parts:
  Part1 = Arduino Uno (Rev3) - ICSP
  Q1 = PHOTOTRANSISTOR REFLECTIVE OBJECT SENSOR [package=qrb1114-side]
  LED1 = RGB LED (com. cathode, rgb) [package="5 mm [THT]"]
  LED2 = smd LED [color="Red (633nm)" package="0603 [SMD]"]
  U1 = POT [package=pot_mammoth]
  S1 = Toggle Switch [package=THT]
  S2 = Toggle Switch [package=THT]
  LCD1 = LCD screen  # not connected
  M1 = DC Motor
  VCC1 = Battery block 9V  # not connected
  Q2 = NPN-Transistor [package="TO92 [THT]"]
  D1 = Rectifier Diode [part_number=1N4001 package="300 mil [THT]"]
  R1 = Resistor [tolerance=±5% resistance=220 package=THT]
  R2 = Resistor [tolerance=±5% resistance=220 package=THT]
  R3 = Resistor [tolerance=±5% resistance=10k package="0603 [SMD]"]

nets:
  N1: Part1.A1, U1.A
  N2: Part1.D9_PWM, LED1.red_anode
  N3: Part1.D10_PWM/SS, LED1.green_anode
  N4: Part1.D11_PWM/MOSI, LED1.blue_anode
  N5: Part1.D13/SCK, R2.Pin_0
  N6: Part1.GND, Q1.A, LED1.common_cathode, LED2.cathode, U1.E, S1.L2, Q2.E, R3.Pin_0
  N7: Part1.D3_PWM, Q1.K
  N8: Part1.D4, S2.L2, R3.Pin_1
  N9: Part1.D6_PWM, R1.Pin_1
  N10: Q1.C, Q1.E, U1.S, S2.COM
  N11: LED2.anode, R2.Pin_1
  N12: M1.pin_1, Q2.C, D1.anode
  N13: M1.pin_2, D1.cathode
  N14: Q2.B, R1.Pin_0

notes:
  The red is 9 volts, the orange is 6 volts
  This battery represents a pack of 6 AA batteries. The motor only needs 6 volts, and so having many smaller batteries allowed us to distribute power correctly
  LCD Backpack
